# Fritzing sketch Arduino_sketch (saved by Fritzing 0.9.3b)
circuit board: 8.46667cm x 5.64444cm
breadboards: 3

parts:
  Arduino = Arduino Nano 33 IOT
  Right_IR_sensor = 2E10 IR Infrared Sensor Module
  Left_IR-sensor = 2E10 IR Infrared Sensor Module
  Ultra-sonic_sensor = hc-sr04
  Left_Moter = DC Motor
  Right_moter = DC Motor
  H-Bridge = L293D [package=THT]

nets:
  GND: Arduino.GND, Right_IR_sensor.GND, Left_IR-sensor.GND, Ultra-sonic_sensor.GND, H-Bridge.0V
  N1: Arduino.D2, Left_IR-sensor.D0
  N2: Arduino.D3~, Right_IR_sensor.D0
  N3: Arduino.D9~, H-Bridge.In_1
  N4: Arduino.D10~, H-Bridge.In_2
  N5: Arduino.D11/MOSI, H-Bridge.In_3
  N6: Arduino.D12~/MISO, H-Bridge.In_4
  N7: Arduino.A3, H-Bridge.Enable_1
  N8: Arduino.A2, H-Bridge.Enable_2
  N9: Arduino.A1, Ultra-sonic_sensor.Trig
  N10: Arduino.A0, Ultra-sonic_sensor.Echo
  VCC: Arduino.3V3, Right_IR_sensor.VCC, Left_IR-sensor.VCC, Ultra-sonic_sensor.VCC
  N11: Arduino.+5V, H-Bridge.+Vmotor, H-Bridge.+V
  N12: Left_Moter.pin_1, H-Bridge.Out_1_(_Controlled_by_Enable_1_)
  N13: Left_Moter.pin_2, H-Bridge.Out_2_(_Controlled_by_Enable_1_)
  N14: Right_moter.pin_1, H-Bridge.Out_4_(_Controlled_by_Enable_2_)
  N15: Right_moter.pin_2, H-Bridge.Out_3_(_Controlled_by_Enable_2_)

notes:
  Circuit notes:
  -Ultrasonic sensor is upside down so orange and brown wires swapped.
  - IR-sensors are upside down so brown power lines are swapped
  - for some reason breadboard thinks 22 on uppmost section is connected to D3 so i avoided it
  3.3V rail
  5V rail

custom parts:
  Arduino Nano 33 IOT: The Arduino Nano 33 IoT is the easiest and cheapest point of entry to enhance existing devices (and creating new ones) to be part of the IoT and designing pico-network applications. Whether you are looking at building a sensor network connected to your office or home router, or if you want to create a BLE device sending data to a cellphone, the Nano 33 IoT is your one-stop-solution for many of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
  2E10 IR Infrared Sensor Module: An infrared obstacle detector, with analogue & digital output
